# Fritzing sketch Drone_JoyStick_proto (saved by Fritzing 1.0.2b)

parts:
  Part1 = Thumb Joystick
  U1 = Nanit [package=_]
  U2 = Adapter Nanit [package=rf24g-2x5]
  Part2 = Thumb Joystick
  U3 = Adapter Nanit [package=rf24g-2x5]
  Part3 = NRF24L01+

nets:
  GND: Part1.GND, U2.GND
  N1: Part1.SEL, U2.4
  N2: Part1.HORZ, U2.3
  N3: Part1.VERT, U2.2
  VCC: Part1.VCC, U2.VCC
  N4: U1.Port_#6, U2.Port
  N5: U1.Port_#7, U3.Port
  N6: U1.VCC_SPI, Part3.VCC
  N7: U1.MISO_SPI, Part3.MOSI
  N8: U1.MOSI_SPI, Part3.MISO
  N9: U1.SCK_SPI, Part3.SCK
  N10: U1.GND_SPI, Part3.GND
  N11: U2.1, Part3.CS
  GND_2: Part2.GND, U3.GND
  N12: Part2.SEL, U3.3
  N13: Part2.HORZ, U3.2
  N14: Part2.VERT, U3.1
  VCC_2: Part2.VCC, U3.VCC
  N15: U3.4, Part3.CE

custom parts:
  Nanit: Nanit 3.4
  Adapter Nanit: Adapter
